# Fritzing sketch base_tx (saved by Fritzing 0.9.3b)
breadboards: 1

parts:
  Часть5 = nrf73
  Часть1 = BluePill  # not connected
  U1 = POT [package=pot_alpha_rv16af-20]
  U2 = POT [package=pot_alpha_rv16af-20]
  VCC1 = 4 x AAA Battery Mount

nets:
  N1: Часть5.VCC, U1.E, U2.E
  N2: Часть5.GND, U1.A, U2.A, VCC1.-

custom parts:
  nrf73: 2.4 Ghz rfm73 module
